# Fritzing sketch GP2Y0A710K0F (saved by Fritzing 0.9.2b)
breadboards: 1

parts:
  パーツ1 = Arduino Mega ADK (Rev3)
  U1 = GP2Y0A710K0F [package=to-92-kit]

nets:
  N1: パーツ1.A0, U1.VOUT
  5V: パーツ1.5V, U1.VCC
  GND: パーツ1.GND, U1.GND
