# Fritzing sketch GP2Y0A710K0F_SSCI-014007breadboard (saved by Fritzing 0.9.2b)
breadboards: 1

parts:
  パーツ1 = Arduino Mega ADK (Rev3)
  U1 = GP2Y0A710K0F [package=to-92-kit]
  NEOPIXEL1 = Neopixel Strip -- White (60/m)

nets:
  N1: パーツ1.A0, U1.VOUT
  5V: パーツ1.5V, U1.VCC, NEOPIXEL1.DI
  GND: パーツ1.GND, U1.GND, NEOPIXEL1.GND
  N2: パーツ1.D6_PWM, NEOPIXEL1.+5V

custom parts:
  Neopixel Strip -- White (60/m): Neopixel Strip, White, 60 pixels per meter.
