# Fritzing sketch all_sensors (saved by Fritzing 0.9.2b)
breadboards: 1

parts:
  パーツ1 = Arduino Mega ADK (Rev3)
  Raspberry_Pi1 = Raspberry Pi B+  # not connected
  U1 = GP2Y0A710K0F [package=to-92-kit]
  IR1 = SE-10 [package=THT]
  R1 = Resistor [tolerance=±5% resistance=1k package=THT]
  NEOPIXEL2 = Neopixel Strip -- White (60/m)
  T1 = LM35 Temperature Sensor [package="TO92 [THT]"]

nets:
  N1: パーツ1.A15, T1.+Vs
  N2: パーツ1.A0, U1.VOUT
  5V: パーツ1.5V, U1.VCC, IR1.+B, R1.Pin_0, NEOPIXEL2.DI
  GND: パーツ1.GND, U1.GND, IR1.GND, NEOPIXEL2.GND
  N3: パーツ1.D2_PWM, IR1.ALARM, R1.Pin_1
  N4: パーツ1.D6_PWM, NEOPIXEL2.+5V

custom parts:
  SE-10: The TSOP312.., TSOP314.. series are miniaturized receivers for infrared remote control systems. A PIN diode and a preamplifier are assembled on a lead frame, the epoxy package acts as an IR filter. The demodulated output signal can be directly decoded by a microprocessor. The TSOP312.. is compatible with all common IR remote control data formats. The TSOP314.. is optimized to suppress almost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
  Neopixel Strip -- White (60/m): Neopixel Strip, White, 60 pixels per meter.
