# Fritzing sketch se-10 (saved by Fritzing 0.9.2b)
breadboards: 1

parts:
  パーツ1 = Arduino Mega ADK (Rev3)
  IR1 = SE-10 [package=THT]
  R1 = Resistor [tolerance=±5% resistance=1k package=THT]

nets:
  N1: パーツ1.5V, IR1.+B, R1.Pin_0
  GND: パーツ1.GND, IR1.GND
  N2: パーツ1.D2_PWM, IR1.ALARM, R1.Pin_1

custom parts:
  SE-10: The TSOP312.., TSOP314.. series are miniaturized receivers for infrared remote control systems. A PIN diode and a preamplifier are assembled on a lead frame, the epoxy package acts as an IR filter. The demodulated output signal can be directly decoded by a microprocessor. The TSOP312.. is compatible with all common IR remote control data formats. The TSOP314.. is optimized to suppress almost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
